# Fritzing sketch fritzing_stepper_test (saved by Fritzing 0.9.3b)
breadboards: 1

parts:
  Bauteil1 = Arduino Uno (Rev3)
  DRV_1 = DRV 8825 Stepper Motor Carrier, High Current [part_number="DRV 8825"]
  M2 = Stepper Motor - Bipolar
  C1 = Electrolytic Capacitor [capacitance=1µF package="100 mil [THT, electrolytic]"]

nets:
  N1: Bauteil1.D13/SCK, DRV_1.MS3, DRV_1.RESET
  N2: Bauteil1.GND, DRV_1.GROUND_LOG
  N3: DRV_1.VOLTAGE_ST/_MT, C1.-
  N4: DRV_1.GROUND_ST/_MT, C1.+
  N5: DRV_1.OUT_2B, M2.C
  N6: DRV_1.OUT_2A, M2.D
  N7: DRV_1.OUT_1A, M2.A
  N8: DRV_1.OUT_1B, M2.B

notes:
  24V DC
